# Fritzing sketch Controlling LED by Button (saved by Fritzing 0.8.7b)
breadboards: 1

parts:
  R2 = Resistor [tolerance=±5% resistance=10k package=THT]
  KEY = Pushbutton [package="[THT]"]
  KEY_2 = Arduino Uno (Rev3)

nets:
  N1: R2.Pin_0, KEY_2.GND
  N2: R2.Pin_1, KEY.Pin_3, KEY.Pin_4, KEY_2.D12/MISO
  N3: KEY.Pin_1, KEY.Pin_2, KEY_2.5V
