# Fritzing sketch Untitled Sketch (saved by Fritzing 0.8.7b)
breadboards: 1

parts:
  元件1 = Arduino Uno (Rev3)
  R1 = Photocell (LDR) [package=THT]
  R2 = Resistor [tolerance=±5% resistance=10k package=THT]
  J1 = Piezo Speaker

nets:
  N1: 元件1.A0, R1.pin_0, R2.Pin_1
  N2: 元件1.D9_PWM, J1.pin2
  N3: 元件1.GND, R2.Pin_0, J1.pin1
  N4: 元件1.5V, R1.pin_1
