# Fritzing sketch 7-Segment Display (saved by Fritzing 0.8.7b)
breadboards: 1

parts:
  元件1 = Arduino Uno (Rev3)
  R1 = Resistor [tolerance=±5% resistance=220 package=THT]
  R2 = Resistor [tolerance=±5% resistance=220 package=THT]
  R3 = Resistor [tolerance=±5% resistance=220 package=THT]
  R4 = Resistor [tolerance=±5% resistance=220 package=THT]
  R5 = Resistor [tolerance=±5% resistance=220 package=THT]
  R6 = Resistor [tolerance=±5% resistance=220 package=THT]
  R7 = Resistor [tolerance=±5% resistance=220 package=THT]
  R8 = Resistor [tolerance=±5% resistance=220 package=THT]
  DI1 = 7-Segment LED Display [package=THT]

nets:
  N1: 元件1.D8, R3.Pin_0
  N2: 元件1.D9_PWM, R4.Pin_0
  N3: 元件1.D10_PWM/SS, R6.Pin_0
  N4: 元件1.D11_PWM/MOSI, R5.Pin_0
  N5: 元件1.GND, DI1.commAnode#2
  N6: 元件1.D4, R7.Pin_1
  N7: 元件1.D5_PWM, R8.Pin_1
  N8: 元件1.D6_PWM, R1.Pin_1
  N9: 元件1.D7, R2.Pin_1
  N10: R1.Pin_0, DI1.cathodeB
  N11: R2.Pin_0, DI1.cathodeA
  N12: R3.Pin_1, DI1.cathodeF
  N13: R4.Pin_1, DI1.cathodeG
  N14: R5.Pin_1, DI1.cathodeD
  N15: R6.Pin_1, DI1.cathodeE
  N16: R7.Pin_0, DI1.cathodeDP
  N17: R8.Pin_0, DI1.cathodeC
