# Fritzing sketch Dot-matrix Display (saved by Fritzing 0.8.7b)
breadboards: 1

parts:
  元件1 = Arduino Uno (Rev3)
  U1 = 74HC595 [package="DIP16 [THT]"]
  U3 = 74HC595 [package="DIP16 [THT]"]
  元件2 = LED Matrix - Serial Interface - Red/Green/Blue
  R1 = Resistor [tolerance=±5% resistance=220 package=THT]
  R2 = Resistor [tolerance=±5% resistance=220 package=THT]
  R3 = Resistor [tolerance=±5% resistance=220 package=THT]
  R4 = Resistor [tolerance=±5% resistance=220 package=THT]
  R5 = Resistor [tolerance=±5% resistance=220 package=THT]
  R6 = Resistor [tolerance=±5% resistance=220 package=THT]
  R7 = Resistor [tolerance=±5% resistance=220 package=THT]
  R8 = Resistor [tolerance=±5% resistance=220 package=THT]

nets:
  N1: 元件1.D8, U1.ST_CP, U3.ST_CP
  N2: 元件1.D11_PWM/MOSI, U3.DS
  N3: 元件1.D12/MISO, U1.SH_CP, U3.SH_CP
  GND: 元件1.GND, U1.Q1, U1.GND, U3.GND, R4.Pin_0
  N4: U1.Q2, R3.Pin_0
  N5: U1.Q3, R7.Pin_0
  N6: U1.Q4, R8.Pin_0
  N7: U1.Q5, R2.Pin_0
  N8: U1.Q6, R1.Pin_0
  N9: U1.Q7, R5.Pin_0
  VCC: U1.MR, U1.VCC, U3.MR, U3.VCC
  N10: U1.OE, U3.OE
  N11: U1.DS, U3.Q7'
  N12: U1.Q0, R6.Pin_0
  N13: U3.Q1, U3.Q6, 元件2.VCC, R1.Pin_1, R4.Pin_1
  N14: U3.Q2, 元件2.MOSI
  N15: U3.Q3, 元件2.MISO
  N16: U3.Q4, 元件2.GND, R3.Pin_1
  N17: U3.Q5, U3.Q7, 元件2.SCK
  N18: 元件2.CS, R6.Pin_1, R8.Pin_1
