# Fritzing sketch buzzer (saved by Fritzing 0.8.7b)
circuit board: 8.46667cm x 5.64444cm
breadboards: 1

parts:
  元件1 = Arduino Uno (Rev3)
  J1 = Piezo Speaker

nets:
  N1: 元件1.D12/MISO, J1.pin2
  N2: 元件1.GND, J1.pin1
