# Fritzing sketch Tilt_Switch (saved by Fritzing 0.8.7b)
breadboards: 1

parts:
  tilt_switch = Arduino Uno (Rev3)
  S1 = Tilt Switch [package=THT]

nets:
  N1: tilt_switch.GND, S1.Pin_1
  N2: tilt_switch.D2, S1.Pin_2
