# Fritzing sketch responder (saved by Fritzing 0.8.7b)
breadboards: 1

parts:
  元件1 = Arduino Uno (Rev3)
  S1 = Pushbutton [package="[THT]"]
  S2 = Pushbutton [package="[THT]"]
  S3 = Pushbutton [package="[THT]"]
  S4 = Pushbutton [package="[THT]"]
  LED1 = LED - 5mm [color="White (4500K)" package="5 mm [THT]"]
  LED2 = LED - 5mm [color="White (4500K)" package="5 mm [THT]"]
  LED3 = LED - 5mm [color="White (4500K)" package="5 mm [THT]"]
  LED4 = LED - 5mm [color="White (4500K)" package="5 mm [THT]"]
  R1 = Resistor [tolerance=±5% resistance=220 package=THT]
  R2 = Resistor [tolerance=±5% resistance=220 package=THT]
  R3 = Resistor [tolerance=±5% resistance=220 package=THT]
  R4 = Resistor [tolerance=±5% resistance=220 package=THT]
  J1 = Piezo Speaker

nets:
  N1: 元件1.D8, R4.Pin_0
  N2: 元件1.D9_PWM, S4.Pin_1, S4.Pin_2
  N3: 元件1.D10_PWM/SS, R1.Pin_0
  N4: 元件1.GND, S1.Pin_3, S1.Pin_4, S2.Pin_1, S2.Pin_2, S3.Pin_1, S3.Pin_2, S4.Pin_3, S4.Pin_4, LED1.cathode, LED2.cathode, LED3.cathode, LED4.cathode, J1.pin1
  N5: 元件1.D2, S2.Pin_3, S2.Pin_4
  N6: 元件1.D3_PWM, S3.Pin_3, S3.Pin_4
  N7: 元件1.D4, S1.Pin_1, S1.Pin_2
  N8: 元件1.D5_PWM, J1.pin2
  N9: 元件1.D6_PWM, R3.Pin_0
  N10: 元件1.D7, R2.Pin_0
  N11: LED1.anode, R2.Pin_1
  N12: LED2.anode, R4.Pin_1
  N13: LED3.anode, R1.Pin_1
  N14: LED4.anode, R3.Pin_1
