# Fritzing sketch Serial Monitor (saved by Fritzing 0.8.7b)
breadboards: 1

parts:
  元件1 = Arduino Uno (Rev3)
  R1 = Resistor [tolerance=±5% resistance=220 package=THT]
  R2 = Resistor [tolerance=±5% resistance=220 package=THT]
  R3 = Resistor [tolerance=±5% resistance=220 package=THT]
  LED4 = LED - 5mm [color="White (4500K)" package="5 mm [THT]"]
  LED5 = LED - 5mm [color="White (4500K)" package="5 mm [THT]"]
  LED6 = LED - 5mm [color="White (4500K)" package="5 mm [THT]"]

nets:
  N1: 元件1.GND, LED4.cathode, LED5.cathode, LED6.cathode
  N2: 元件1.D2, R3.Pin_0
  N3: 元件1.D3_PWM, R2.Pin_0
  N4: 元件1.D4, R1.Pin_0
  N5: R1.Pin_1, LED5.anode
  N6: R2.Pin_1, LED4.anode
  N7: R3.Pin_1, LED6.anode
