# Fritzing sketch photocell (saved by Fritzing 0.8.7b)
breadboards: 1

parts:
  元件1 = Arduino Uno (Rev3)
  LED2 = LED - 5mm [color="White (8000K)" package="5 mm [THT]"]
  R4 = Resistor [tolerance=±5% resistance=220 package=THT]
  R5 = Photocell (LDR) [package=THT]
  R6 = Resistor [tolerance=±5% resistance=10k package=THT]
  LED3 = LED - 5mm [color="White (8000K)" package="5 mm [THT]"]
  LED4 = LED - 5mm [color="White (8000K)" package="5 mm [THT]"]
  LED5 = LED - 5mm [color="White (8000K)" package="5 mm [THT]"]
  LED6 = LED - 5mm [color="White (8000K)" package="5 mm [THT]"]
  LED7 = LED - 5mm [color="White (8000K)" package="5 mm [THT]"]
  LED8 = LED - 5mm [color="White (8000K)" package="5 mm [THT]"]
  R7 = Resistor [tolerance=±5% resistance=220 package=THT]
  R8 = Resistor [tolerance=±5% resistance=220 package=THT]
  R9 = Resistor [tolerance=±5% resistance=220 package=THT]
  R10 = Resistor [tolerance=±5% resistance=220 package=THT]
  R11 = Resistor [tolerance=±5% resistance=220 package=THT]
  R12 = Resistor [tolerance=±5% resistance=220 package=THT]
  R13 = Resistor [tolerance=±5% resistance=220 package=THT]
  LED9 = LED - 5mm [color="White (8000K)" package="5 mm [THT]"]

nets:
  N1: 元件1.A0, R5.pin_1, R6.Pin_0
  N2: 元件1.D8, R10.Pin_0
  N3: 元件1.D9_PWM, R9.Pin_0
  N4: 元件1.D10_PWM/SS, R8.Pin_0
  N5: 元件1.D11_PWM/MOSI, R7.Pin_0
  N6: 元件1.D12/MISO, R4.Pin_0
  N7: 元件1.GND, LED2.cathode, R6.Pin_1, LED3.cathode, LED4.cathode, LED5.cathode, LED6.cathode, LED7.cathode, LED8.cathode, LED9.cathode
  N8: 元件1.D5_PWM, R13.Pin_0
  N9: 元件1.D6_PWM, R12.Pin_0
  N10: 元件1.D7, R11.Pin_0
  N11: 元件1.5V, R5.pin_0
  N12: LED2.anode, R4.Pin_1
  N13: LED3.anode, R7.Pin_1
  N14: LED4.anode, R9.Pin_1
  N15: LED5.anode, R12.Pin_1
  N16: LED6.anode, R11.Pin_1
  N17: LED7.anode, R8.Pin_1
  N18: LED8.anode, R10.Pin_1
  N19: R13.Pin_1, LED9.anode
